// Logisim project lab2.circ as structural Verilog: 1 circuit, main circuit main
module main (
  input  in_1,
  input  in_2,
  input  in_3,
  input  in_4,
  input  in_5,
  input  in_6,
  input  in_7,
  input  in_8,
  input  in_9,
  input  in_10,
  input  in_11,
  input  in_12,
  input  in_13,
  input  in_14,
  input  in_15,
  input  in_16,
  input  in_17,
  input  in_18,
  input  in_19,
  input  in_20,
  output out_21,
  output out_22,
  output out_23,
  output out_24,
  output out_25
);

  wire and_1_out, and_2_out, and_3_out, and_4_out, and_5_out, and_6_out, and_7_out, and_9_out, and_10_out,
       and_11_out, and_12_out, and_13_out, and_14_out, and_15_out, not_1_out, not_2_out, not_3_out,
       not_4_out, not_5_out, not_6_out, not_7_out, not_8_out, not_9_out, not_10_out, not_11_out, not_12_out,
       not_13_out, not_14_out, not_15_out, not_16_out, not_17_out, not_18_out, not_19_out, or_2_out,
       or_3_out, or_4_out, or_6_out, or_7_out, or_8_out, or_9_out, or_10_out, or_11_out, or_12_out, or_13_out;

  not not_1 (not_1_out, in_9);
  not not_2 (not_2_out, in_10);
  not not_3 (not_3_out, in_12);
  not not_4 (not_4_out, in_13);
  and and_1 (and_1_out, in_9, in_10);
  and and_2 (and_2_out, not_2_out, in_11);
  and and_3 (and_3_out, in_9, in_11);
  and and_4 (and_4_out, not_1_out, in_10, not_3_out);
  not not_5 (not_5_out, in_14);
  not not_6 (not_6_out, in_15);
  or or_1 (out_22, and_1_out, and_2_out, and_3_out, and_4_out);
  not not_7 (not_7_out, in_16);
  or or_2 (or_2_out, not_4_out, in_14);
  or or_3 (or_3_out, not_7_out, in_15);
  and and_5 (and_5_out, in_13, not_5_out);
  and and_6 (and_6_out, in_16, not_6_out);
  and and_7 (and_7_out, or_2_out, or_3_out);
  or or_4 (or_4_out, and_5_out, and_6_out);
  and and_8 (out_25, and_7_out, or_4_out);
  not not_8 (not_8_out, in_1);
  not not_9 (not_9_out, in_2);
  not not_10 (not_10_out, in_3);
  not not_11 (not_11_out, in_4);
  not not_12 (not_12_out, in_18);
  not not_13 (not_13_out, in_17);
  and and_9 (and_9_out, in_1, in_2, in_3, in_4);
  and and_10 (and_10_out, in_1, not_9_out, in_3, in_4);
  and and_11 (and_11_out, not_8_out, in_2, in_3, in_4);
  and and_12 (and_12_out, in_1, in_2, not_10_out, in_4);
  and and_13 (and_13_out, in_1, in_2, in_3, not_11_out);
  not not_14 (not_14_out, in_19);
  not not_15 (not_15_out, in_20);
  or or_5 (out_21, and_9_out, and_10_out, and_11_out, and_12_out, and_13_out);
  or or_6 (or_6_out, in_20, in_19);
  or or_7 (or_7_out, not_15_out, not_14_out);
  and and_14 (and_14_out, in_18, or_6_out);
  and and_15 (and_15_out, in_18, or_7_out);
  not not_16 (not_16_out, in_5);
  or or_8 (or_8_out, in_17, and_14_out);
  or or_9 (or_9_out, not_13_out, and_15_out);
  not not_17 (not_17_out, in_6);
  not not_18 (not_18_out, in_7);
  and and_16 (out_24, or_8_out, or_9_out);
  not not_19 (not_19_out, in_8);
  or or_10 (or_10_out, in_5, in_6, in_7, in_8);
  or or_11 (or_11_out, in_5, in_6, not_18_out);
  or or_12 (or_12_out, in_5, not_17_out, in_7);
  or or_13 (or_13_out, not_16_out, in_6, in_7);
  and and_17 (out_23, or_10_out, or_11_out, or_12_out, or_13_out);

  // Notes on the sheet:
  //   F = AB + B̄C + AC + ĀBD̄
  //   EQUATION1
  //   F = [(Ā+B)(C+D̄)] · [AB̄ + (C̄D)]
  //   EQUATION 2
  //   F = ABCD + AB̄CD + ĀBCD + ABC̄D + ABCD̄
  //   EQUATION 3
  //   F = [A + B̄(C+D)] · [Ā+B(C̄+D̄)]
  //   EQUATION 5
  //   F = (A+B+C+D)(A+B+C̄)(A+B̄+C)(Ā+B+C)
  //   EQUATION 3
endmodule
